# Fritzing sketch Scheme (saved by Fritzing 0.9.3b)

parts:
  Часть1 = Arduino Nano (Rev3.0)
  R1 = Resistor [tolerance=±5% resistance=100 package=THT]
  R2 = Resistor [tolerance=±5% resistance=100 package=THT]
  R3 = Resistor [tolerance=±5% resistance=100 package=THT]
  R4 = Resistor [tolerance=±5% resistance=68 package=THT]
  R5 = Resistor [tolerance=±5% resistance=100 package=THT]
  R6 = Resistor [tolerance=±5% resistance=100 package=THT]
  R7 = Resistor [tolerance=±5% resistance=100 package=THT]
  R8 = Resistor [tolerance=±5% resistance=100 package=THT]
  DI1 = 7-Segment LED Display [package=THT]
  U1 = POT_SWITCH [package=pot_pth_switch]

nets:
  N1: Часть1.GND, DI1.commAnode, U1.G$1_A
  N2: Часть1.D2, R3.Pin_0
  N3: Часть1.D3, R4.Pin_0
  N4: Часть1.D4, R8.Pin_1
  N5: Часть1.D5, R6.Pin_1
  N6: Часть1.D6, R5.Pin_1
  N7: Часть1.D7, R2.Pin_0
  N8: Часть1.D8, R1.Pin_0
  N9: Часть1.D9, R7.Pin_1
  N10: Часть1.5V, U1.G$2_2
  N11: Часть1.A0, U1.G$2_1
